# Fritzing sketch CompleteSchema (saved by Fritzing 0.9.3b)
breadboards: 1

parts:
  Arduino_GSM_Shield_V2 = Arduino GSM Shield
  Arduino_Uno_R3 = Arduino Uno (Rev3)  # not connected
  Senzor_Magnetic_2 = HALL-EFFECT [package=sc70]
  Senzor_Magnetic_1 = HALL-EFFECT [package=sc70]
  Breadboard_Power_Supply = USB Connectors [package=usb-a-s-nosilk]
  Senzor_Detecție_Gaz = GAS_SENSOR [package=mq-9]
  Senzor_Ultrasonic_1 = hc-sr04
  Senzor_Ultrasonic_2 = hc-sr04
  Speaker/Buzzer = SPEAKER [package=pcb_mount_speaker]
  Tastatura = KEYPAD 4x4
  part = Resistor [tolerance=±5% resistance=4.7k package=THT]
  part_2 = Resistor [tolerance=±5% resistance=4.7k package=THT]
  part_3 = Resistor [tolerance=±5% resistance=4.7k package=THT]
  part_4 = Resistor [tolerance=±5% resistance=1k package=THT]
  part_5 = Resistor [tolerance=±5% resistance=1k package=THT]
  part_6 = Resistor [tolerance=±5% resistance=1k package=THT]
  part_7 = Resistor [tolerance=±5% resistance=1k package=THT]

nets:
  N1: Arduino_GSM_Shield_V2.AGND, Speaker/Buzzer.+, part_4.Pin_1
  N2: Arduino_GSM_Shield_V2.MOSI/PWM_D11, Senzor_Ultrasonic_1.Trig
  N3: Arduino_GSM_Shield_V2.SS/PWM_D10, Senzor_Ultrasonic_1.Echo
  N4: Arduino_GSM_Shield_V2.PWM_D9, Speaker/Buzzer.-
  N5: Arduino_GSM_Shield_V2.D8, Senzor_Ultrasonic_2.Trig
  N6: Arduino_GSM_Shield_V2.5V, Tastatura.col1, part.Pin_0
  N7: Arduino_GSM_Shield_V2.PWM_D4, Senzor_Magnetic_2.OUT
  N8: Arduino_GSM_Shield_V2.PWM_D5, Senzor_Magnetic_1.OUT
  N9: Arduino_GSM_Shield_V2.PWM_D6, Senzor_Ultrasonic_2.Echo
  N10: Arduino_GSM_Shield_V2.A0, Senzor_Detecție_Gaz.AnalogIn
  N11: Arduino_GSM_Shield_V2.A1, Tastatura.row4, part_4.Pin_0, part_5.Pin_0
  GND: Senzor_Magnetic_2.GND, Senzor_Magnetic_1.GND, Breadboard_Power_Supply.GND, Senzor_Detecție_Gaz.GND, Senzor_Ultrasonic_1.GND, Senzor_Ultrasonic_2.GND
  VCC: Senzor_Magnetic_2.VCC, Senzor_Magnetic_1.VCC, Breadboard_Power_Supply.VBUS, Senzor_Detecție_Gaz.VCC, Senzor_Ultrasonic_1.VCC, Senzor_Ultrasonic_2.VCC
  N12: Tastatura.col2, part.Pin_1, part_2.Pin_0
  N13: Tastatura.col3, part_2.Pin_1, part_3.Pin_0
  N14: Tastatura.col4, part_3.Pin_1
  N15: Tastatura.row1, part_6.Pin_1
  N16: Tastatura.row2, part_6.Pin_0, part_7.Pin_1
  N17: Tastatura.row3, part_5.Pin_1, part_7.Pin_0

custom parts:
  GAS_SENSOR: MQ-9 alcohol gas sensor . FP not tested. SEN-08880.
  KEYPAD 4x4: Matrix keypad 16 buttons, 4 rows x 4 columns
