# Fritzing sketch HC-SR04 (saved by Fritzing 0.9.3b)

parts:
  GSM_Shield_V2 = Arduino GSM Shield
  Arduino_Uno_R3 = Arduino Uno (Rev3)  # not connected
  Ultrasonic_Senzor = hc-sr04

nets:
  N1: GSM_Shield_V2.D8, Ultrasonic_Senzor.Trig
  5V: GSM_Shield_V2.5V, Ultrasonic_Senzor.VCC
  N2: GSM_Shield_V2.AGND, Ultrasonic_Senzor.GND
  N3: GSM_Shield_V2.PWM_D6, Ultrasonic_Senzor.Echo
