# Fritzing sketch Keypad (saved by Fritzing 0.9.3b)
breadboards: 1

parts:
  Arduino_Uno_R3 = Arduino Uno (Rev3)  # not connected
  GSM_Shield_V2 = Arduino GSM Shield
  Tastatura = KEYPAD 4x4
  part = Resistor [tolerance=±5% resistance=4.7k package=THT]
  part_2 = Resistor [tolerance=±5% resistance=4.7k package=THT]
  part_3 = Resistor [tolerance=±5% resistance=4.7k package=THT]
  part_4 = Resistor [tolerance=±5% resistance=1k package=THT]
  part_5 = Resistor [tolerance=±5% resistance=1k package=THT]
  part_6 = Resistor [tolerance=±5% resistance=1k package=THT]
  part_7 = Resistor [tolerance=±5% resistance=1k package=THT]

nets:
  N1: GSM_Shield_V2.5V, Tastatura.row1, part.Pin_0
  N2: GSM_Shield_V2.AGND, part_7.Pin_1
  N3: GSM_Shield_V2.A1, Tastatura.col1, part_4.Pin_0, part_7.Pin_0
  N4: Tastatura.col2, part_4.Pin_1, part_5.Pin_0
  N5: Tastatura.col3, part_5.Pin_1, part_6.Pin_0
  N6: Tastatura.col4, part_6.Pin_1
  N7: Tastatura.row2, part.Pin_1, part_2.Pin_0
  N8: Tastatura.row3, part_2.Pin_1, part_3.Pin_0
  N9: Tastatura.row4, part_3.Pin_1

custom parts:
  KEYPAD 4x4: Matrix keypad 16 buttons, 4 rows x 4 columns
