# Fritzing sketch MQ-9 (saved by Fritzing 0.9.3b)

parts:
  Arduino_Uno_R3 = Arduino Uno (Rev3)  # not connected
  GSM_Shield_V2 = Arduino GSM Shield
  MQ-9_Gas_Senzor = GAS_SENSOR [package=mq-9]

nets:
  5V: GSM_Shield_V2.5V, MQ-9_Gas_Senzor.VCC
  N1: GSM_Shield_V2.AGND, MQ-9_Gas_Senzor.GND
  N2: GSM_Shield_V2.A0, MQ-9_Gas_Senzor.AnalogIn

custom parts:
  GAS_SENSOR: MQ-9 alcohol gas sensor . FP not tested. SEN-08880.
