# Fritzing sketch SS-400 (saved by Fritzing 0.9.3b)

parts:
  Arduino_Uno_R3 = Arduino Uno (Rev3)  # not connected
  GSM_Shield_V2 = Arduino GSM Shield
  Magnetic_Senzor = HALL-EFFECT [package=sc70]

nets:
  5V: GSM_Shield_V2.5V, Magnetic_Senzor.VCC
  N1: GSM_Shield_V2.AGND, Magnetic_Senzor.GND
  N2: GSM_Shield_V2.PWM_D4, Magnetic_Senzor.OUT
